// Logisim project processador.circ as structural Verilog: 25 circuits, main circuit main
module registrador32 (
  input  [31:0] Dado,
  input  CLock,
  input  Seletor,
  output [31:0] Q
);

  wire multiplexer_1_out, multiplexer_2_out, multiplexer_3_out, multiplexer_4_out, multiplexer_5_out,
       multiplexer_6_out, multiplexer_7_out, multiplexer_8_out, multiplexer_9_out, multiplexer_10_out,
       multiplexer_11_out, multiplexer_12_out, multiplexer_13_out, multiplexer_14_out, multiplexer_15_out,
       multiplexer_16_out, multiplexer_17_out, multiplexer_18_out, multiplexer_19_out, multiplexer_20_out,
       multiplexer_21_out, multiplexer_22_out, multiplexer_23_out, multiplexer_24_out, multiplexer_25_out,
       multiplexer_26_out, multiplexer_27_out, multiplexer_28_out, multiplexer_29_out, multiplexer_30_out,
       multiplexer_31_out, multiplexer_32_out;

  Multiplexer multiplexer_1 (.in0(Q[0]), .in1(Dado[0]), .out(multiplexer_1_out), .sel(Seletor));
  Multiplexer multiplexer_2 (.in0(Q[1]), .in1(Dado[1]), .out(multiplexer_2_out), .sel(Seletor));
  Multiplexer multiplexer_3 (.in0(Q[2]), .in1(Dado[2]), .out(multiplexer_3_out), .sel(Seletor));
  Multiplexer multiplexer_4 (.in0(Q[3]), .in1(Dado[3]), .out(multiplexer_4_out), .sel(Seletor));
  Multiplexer multiplexer_5 (.in0(Q[4]), .in1(Dado[4]), .out(multiplexer_5_out), .sel(Seletor));
  Multiplexer multiplexer_6 (.in0(Q[5]), .in1(Dado[5]), .out(multiplexer_6_out), .sel(Seletor));
  Multiplexer multiplexer_7 (.in0(Q[6]), .in1(Dado[6]), .out(multiplexer_7_out), .sel(Seletor));
  Multiplexer multiplexer_8 (.in0(Q[7]), .in1(Dado[7]), .out(multiplexer_8_out), .sel(Seletor));
  Multiplexer multiplexer_9 (.in0(Q[8]), .in1(Dado[8]), .out(multiplexer_9_out), .sel(Seletor));
  Multiplexer multiplexer_10 (.in0(Q[9]), .in1(Dado[9]), .out(multiplexer_10_out), .sel(Seletor));
  Multiplexer multiplexer_11 (.in0(Q[10]), .in1(Dado[10]), .out(multiplexer_11_out), .sel(Seletor));
  Multiplexer multiplexer_12 (.in0(Q[11]), .in1(Dado[11]), .out(multiplexer_12_out), .sel(Seletor));
  Multiplexer multiplexer_13 (.in0(Q[12]), .in1(Dado[12]), .out(multiplexer_13_out), .sel(Seletor));
  Multiplexer multiplexer_14 (.in0(Q[13]), .in1(Dado[13]), .out(multiplexer_14_out), .sel(Seletor));
  Multiplexer multiplexer_15 (.in0(Q[14]), .in1(Dado[14]), .out(multiplexer_15_out), .sel(Seletor));
  Multiplexer multiplexer_16 (.in0(Q[15]), .in1(Dado[15]), .out(multiplexer_16_out), .sel(Seletor));
  Multiplexer multiplexer_17 (.in0(Q[16]), .in1(Dado[16]), .out(multiplexer_17_out), .sel(Seletor));
  Multiplexer multiplexer_18 (.in0(Q[17]), .in1(Dado[17]), .out(multiplexer_18_out), .sel(Seletor));
  Multiplexer multiplexer_19 (.in0(Q[18]), .in1(Dado[18]), .out(multiplexer_19_out), .sel(Seletor));
  Multiplexer multiplexer_20 (.in0(Q[19]), .in1(Dado[19]), .out(multiplexer_20_out), .sel(Seletor));
  Multiplexer multiplexer_21 (.in0(Q[20]), .in1(Dado[20]), .out(multiplexer_21_out), .sel(Seletor));
  Multiplexer multiplexer_22 (.in0(Q[21]), .in1(Dado[21]), .out(multiplexer_22_out), .sel(Seletor));
  Multiplexer multiplexer_23 (.in0(Q[22]), .in1(Dado[22]), .out(multiplexer_23_out), .sel(Seletor));
  Multiplexer multiplexer_24 (.in0(Q[23]), .in1(Dado[23]), .out(multiplexer_24_out), .sel(Seletor));
  Multiplexer multiplexer_25 (.in0(Q[24]), .in1(Dado[24]), .out(multiplexer_25_out), .sel(Seletor));
  Multiplexer multiplexer_26 (.in0(Q[25]), .in1(Dado[25]), .out(multiplexer_26_out), .sel(Seletor));
  Multiplexer multiplexer_27 (.in0(Q[26]), .in1(Dado[26]), .out(multiplexer_27_out), .sel(Seletor));
  Multiplexer multiplexer_28 (.in0(Q[27]), .in1(Dado[27]), .out(multiplexer_28_out), .sel(Seletor));
  Multiplexer multiplexer_29 (.in0(Q[28]), .in1(Dado[28]), .out(multiplexer_29_out), .sel(Seletor));
  Multiplexer multiplexer_30 (.in0(Q[29]), .in1(Dado[29]), .out(multiplexer_30_out), .sel(Seletor));
  Multiplexer multiplexer_31 (.in0(Q[30]), .in1(Dado[30]), .out(multiplexer_31_out), .sel(Seletor));
  Multiplexer multiplexer_32 (.in0(Q[31]), .in1(Dado[31]), .out(multiplexer_32_out), .sel(Seletor));
  flipflop32 FF0 (.Dado(multiplexer_1_out), .Enable(CLock), .Q(Q[0]));  // open: nQ
  flipflop32 FF1 (.Dado(multiplexer_2_out), .Enable(CLock), .Q(Q[1]));  // open: nQ
  flipflop32 FF2 (.Dado(multiplexer_3_out), .Enable(CLock), .Q(Q[2]));  // open: nQ
  flipflop32 FF3 (.Dado(multiplexer_4_out), .Enable(CLock), .Q(Q[3]));  // open: nQ
  flipflop32 FF4 (.Dado(multiplexer_5_out), .Enable(CLock), .Q(Q[4]));  // open: nQ
  flipflop32 FF5 (.Dado(multiplexer_6_out), .Enable(CLock), .Q(Q[5]));  // open: nQ
  flipflop32 FF6 (.Dado(multiplexer_7_out), .Enable(CLock), .Q(Q[6]));  // open: nQ
  flipflop32 FF7 (.Dado(multiplexer_8_out), .Enable(CLock), .Q(Q[7]));  // open: nQ
  flipflop32 FF8 (.Dado(multiplexer_9_out), .Enable(CLock), .Q(Q[8]));  // open: nQ
  flipflop32 FF9 (.Dado(multiplexer_10_out), .Enable(CLock), .Q(Q[9]));  // open: nQ
  flipflop32 FF10 (.Dado(multiplexer_11_out), .Enable(CLock), .Q(Q[10]));  // open: nQ
  flipflop32 FF11 (.Dado(multiplexer_12_out), .Enable(CLock), .Q(Q[11]));  // open: nQ
  flipflop32 FF12 (.Dado(multiplexer_13_out), .Enable(CLock), .Q(Q[12]));  // open: nQ
  flipflop32 FF13 (.Dado(multiplexer_14_out), .Enable(CLock), .Q(Q[13]));  // open: nQ
  flipflop32 FF14 (.Dado(multiplexer_15_out), .Enable(CLock), .Q(Q[14]));  // open: nQ
  flipflop32 FF15 (.Dado(multiplexer_16_out), .Enable(CLock), .Q(Q[15]));  // open: nQ
  flipflop32 FF16 (.Dado(multiplexer_17_out), .Enable(CLock), .Q(Q[16]));  // open: nQ
  flipflop32 FF17 (.Dado(multiplexer_18_out), .Enable(CLock), .Q(Q[17]));  // open: nQ
  flipflop32 FF18 (.Dado(multiplexer_19_out), .Enable(CLock), .Q(Q[18]));  // open: nQ
  flipflop32 FF19 (.Dado(multiplexer_20_out), .Enable(CLock), .Q(Q[19]));  // open: nQ
  flipflop32 FF22 (.Dado(multiplexer_23_out), .Enable(CLock), .Q(Q[22]));  // open: nQ
  flipflop32 FF23 (.Dado(multiplexer_24_out), .Enable(CLock), .Q(Q[23]));  // open: nQ
  flipflop32 FF24 (.Dado(multiplexer_25_out), .Enable(CLock), .Q(Q[24]));  // open: nQ
  flipflop32 FF25 (.Dado(multiplexer_26_out), .Enable(CLock), .Q(Q[25]));  // open: nQ
  flipflop32 FF20 (.Dado(multiplexer_21_out), .Enable(CLock), .Q(Q[20]));  // open: nQ
  flipflop32 FF21 (.Dado(multiplexer_22_out), .Enable(CLock), .Q(Q[21]));  // open: nQ
  flipflop32 FF26 (.Dado(multiplexer_27_out), .Enable(CLock), .Q(Q[26]));  // open: nQ
  flipflop32 FF27 (.Dado(multiplexer_28_out), .Enable(CLock), .Q(Q[27]));  // open: nQ
  flipflop32 FF28 (.Dado(multiplexer_29_out), .Enable(CLock), .Q(Q[28]));  // open: nQ
  flipflop32 FF29 (.Dado(multiplexer_30_out), .Enable(CLock), .Q(Q[29]));  // open: nQ
  flipflop32 FF30 (.Dado(multiplexer_31_out), .Enable(CLock), .Q(Q[30]));  // open: nQ
  flipflop32 FF31 (.Dado(multiplexer_32_out), .Enable(CLock), .Q(Q[31]));  // open: nQ

  // Other names for the same wires on the sheet: Clk = CLock
endmodule

module flipflop32 (
  input  Dado,
  input  Enable,
  output Q,
  output nQ
);

  wire and_1_out, nand_1_out, nand_2_out, nand_3_out, nand_4_out, nand_5_out, not_1_out, not_2_out, not_3_out;

  not not_1 (not_1_out, Dado);
  nand nand_1 (nand_1_out, Dado, Enable);
  and and_1 (and_1_out, Enable, not_1_out);
  not not_2 (not_2_out, and_1_out);
  nand nand_2 (nand_2_out, nand_1_out, nand_3_out);
  nand nand_3 (nand_3_out, nand_2_out, not_2_out);
  not not_3 (not_3_out, Enable);
  nand nand_4 (nand_4_out, nand_2_out, not_3_out);
  nand nand_5 (nand_5_out, not_3_out, nand_3_out);
  nand nand_6 (Q, nand_4_out, nQ);
  nand nand_7 (nQ, Q, nand_5_out);
endmodule

module ComplDois32bitsV2 (
  input  [31:0] in_1,
  output [31:0] out_2
);

  wire not_1_out, not_2_out, not_3_out, not_4_out, not_5_out, not_6_out, not_7_out, not_8_out, not_9_out,
       not_10_out, not_11_out, not_12_out, not_13_out, not_14_out, not_15_out, not_16_out, not_17_out,
       not_18_out, not_19_out, not_20_out, not_21_out, not_22_out, not_23_out, not_24_out, not_25_out,
       not_26_out, not_27_out, not_28_out, not_29_out, not_30_out, not_31_out, not_32_out, not_33_out,
       not_34_out, not_35_out, not_36_out, not_37_out, not_38_out, not_39_out, not_40_out, not_41_out,
       not_42_out, not_43_out, not_44_out, not_45_out, not_46_out, not_47_out, not_48_out, not_49_out,
       not_50_out, not_51_out, not_52_out, not_53_out, not_54_out, not_55_out, not_56_out, not_57_out,
       not_58_out, not_59_out, not_60_out, not_61_out, not_62_out;

  not not_1 (not_1_out, in_1[0]);
  not not_2 (not_2_out, in_1[1]);
  not not_3 (not_3_out, out_2[1]);
  not not_4 (not_4_out, in_1[2]);
  not not_5 (not_5_out, out_2[2]);
  not not_6 (not_6_out, in_1[3]);
  not not_7 (not_7_out, out_2[3]);
  not not_8 (not_8_out, in_1[4]);
  not not_9 (not_9_out, out_2[4]);
  not not_10 (not_10_out, in_1[5]);
  not not_11 (not_11_out, out_2[5]);
  not not_12 (not_12_out, in_1[6]);
  not not_13 (not_13_out, out_2[6]);
  not not_14 (not_14_out, in_1[7]);
  not not_15 (not_15_out, out_2[7]);
  not not_16 (not_16_out, in_1[8]);
  not not_17 (not_17_out, out_2[8]);
  not not_18 (not_18_out, in_1[9]);
  not not_19 (not_19_out, out_2[9]);
  not not_20 (not_20_out, in_1[10]);
  not not_21 (not_21_out, out_2[10]);
  not not_22 (not_22_out, in_1[11]);
  not not_23 (not_23_out, out_2[11]);
  not not_24 (not_24_out, in_1[12]);
  not not_25 (not_25_out, out_2[12]);
  not not_26 (not_26_out, in_1[13]);
  not not_27 (not_27_out, out_2[13]);
  not not_28 (not_28_out, in_1[14]);
  not not_29 (not_29_out, out_2[14]);
  not not_30 (not_30_out, in_1[15]);
  not not_31 (not_31_out, out_2[15]);
  not not_32 (not_32_out, in_1[16]);
  not not_33 (not_33_out, out_2[16]);
  not not_34 (not_34_out, in_1[17]);
  not not_35 (not_35_out, out_2[17]);
  not not_36 (not_36_out, in_1[18]);
  not not_37 (not_37_out, out_2[18]);
  not not_38 (not_38_out, in_1[19]);
  not not_39 (not_39_out, out_2[19]);
  not not_40 (not_40_out, in_1[20]);
  not not_41 (not_41_out, out_2[20]);
  not not_42 (not_42_out, in_1[21]);
  not not_43 (not_43_out, out_2[21]);
  not not_44 (not_44_out, in_1[22]);
  not not_45 (not_45_out, out_2[22]);
  not not_46 (not_46_out, in_1[23]);
  not not_47 (not_47_out, out_2[23]);
  not not_48 (not_48_out, in_1[24]);
  not not_49 (not_49_out, out_2[24]);
  not not_50 (not_50_out, in_1[25]);
  not not_51 (not_51_out, out_2[25]);
  not not_52 (not_52_out, in_1[26]);
  not not_53 (not_53_out, out_2[26]);
  not not_54 (not_54_out, in_1[27]);
  not not_55 (not_55_out, out_2[27]);
  not not_56 (not_56_out, in_1[28]);
  not not_57 (not_57_out, out_2[28]);
  not not_58 (not_58_out, in_1[29]);
  not not_59 (not_59_out, out_2[29]);
  not not_60 (not_60_out, in_1[30]);
  not not_61 (not_61_out, out_2[30]);
  not not_62 (not_62_out, in_1[31]);
  xor xor_1 (out_2[1], not_1_out, not_2_out);
  xor xor_2 (out_2[2], not_3_out, not_4_out);
  xor xor_3 (out_2[3], not_5_out, not_6_out);
  xor xor_4 (out_2[4], not_7_out, not_8_out);
  xor xor_5 (out_2[5], not_9_out, not_10_out);
  xor xor_6 (out_2[6], not_11_out, not_12_out);
  xor xor_7 (out_2[7], not_13_out, not_14_out);
  xor xor_8 (out_2[8], not_15_out, not_16_out);
  xor xor_9 (out_2[9], not_17_out, not_18_out);
  xor xor_10 (out_2[10], not_19_out, not_20_out);
  xor xor_11 (out_2[11], not_21_out, not_22_out);
  xor xor_12 (out_2[12], not_23_out, not_24_out);
  xor xor_13 (out_2[13], not_25_out, not_26_out);
  xor xor_14 (out_2[14], not_27_out, not_28_out);
  xor xor_15 (out_2[15], not_29_out, not_30_out);
  xor xor_16 (out_2[16], not_31_out, not_32_out);
  xor xor_17 (out_2[17], not_33_out, not_34_out);
  xor xor_18 (out_2[18], not_35_out, not_36_out);
  xor xor_19 (out_2[19], not_37_out, not_38_out);
  xor xor_20 (out_2[20], not_39_out, not_40_out);
  xor xor_21 (out_2[21], not_41_out, not_42_out);
  xor xor_22 (out_2[22], not_43_out, not_44_out);
  xor xor_23 (out_2[23], not_45_out, not_46_out);
  xor xor_24 (out_2[24], not_47_out, not_48_out);
  xor xor_25 (out_2[25], not_49_out, not_50_out);
  xor xor_26 (out_2[26], not_51_out, not_52_out);
  xor xor_27 (out_2[27], not_53_out, not_54_out);
  xor xor_28 (out_2[28], not_55_out, not_56_out);
  xor xor_29 (out_2[29], not_57_out, not_58_out);
  xor xor_30 (out_2[30], not_59_out, not_60_out);
  xor xor_31 (out_2[31], not_61_out, not_62_out);

  assign out_2[0] = in_1[0];
endmodule

module FlipFlopD (
  input  Dado,
  input  Enable,
  output out_3,
  output out_4
);

  wire and_1_out, nand_1_out, nand_2_out, nand_3_out, nand_4_out, nand_5_out, not_1_out, not_2_out, not_3_out;

  not not_1 (not_1_out, Dado);
  nand nand_1 (nand_1_out, Dado, Enable);
  and and_1 (and_1_out, Enable, not_1_out);
  not not_2 (not_2_out, and_1_out);
  nand nand_2 (nand_2_out, nand_1_out, nand_3_out);
  nand nand_3 (nand_3_out, nand_2_out, not_2_out);
  not not_3 (not_3_out, Enable);
  nand nand_4 (nand_4_out, nand_2_out, not_3_out);
  nand nand_5 (nand_5_out, not_3_out, nand_3_out);
  nand nand_6 (out_3, nand_4_out, out_4);
  nand nand_7 (out_4, out_3, nand_5_out);
endmodule

module FullAdder (
  input  Ax,
  input  Bx,
  input  Cin,
  output Sx,
  output Cout
);

  wire and_1_out, and_2_out, xor_1_out;

  xor xor_1 (xor_1_out, Ax, Bx);
  xor xor_2 (Sx, xor_1_out, Cin);
  and and_1 (and_1_out, xor_1_out, Cin);
  and and_2 (and_2_out, Bx, Ax);
  or or_1 (Cout, and_1_out, and_2_out);
endmodule

module HalfAdder (
  input  A0,
  input  B0,
  output Cout,
  output S0
);

  and and_1 (Cout, A0, B0);
  xor xor_1 (S0, A0, B0);
endmodule

module Shifter32bits (
  input  S
);

  wire and_1_out, and_2_out, and_3_out, and_4_out, and_5_out, and_6_out, and_7_out, and_8_out, and_9_out,
       and_10_out, and_11_out, and_12_out, and_13_out, and_14_out, and_15_out, and_16_out, and_17_out,
       and_18_out, and_19_out, and_20_out, and_21_out, and_22_out, and_23_out, and_24_out, and_25_out,
       and_26_out, and_27_out, and_28_out, and_29_out, and_30_out, and_31_out, and_32_out, and_33_out,
       and_34_out, and_35_out, and_36_out, and_37_out, and_38_out, and_39_out, and_40_out, and_41_out,
       and_42_out, and_43_out, and_44_out, and_45_out, and_46_out, and_47_out, and_48_out, and_49_out,
       and_50_out, and_51_out, and_52_out, and_53_out, and_54_out, and_55_out, and_56_out, and_57_out,
       and_58_out, and_59_out, and_60_out, and_61_out, and_62_out, and_63_out, and_64_out, not_1_out,
       not_2_out, not_3_out, not_4_out, not_5_out, not_6_out, not_7_out, not_8_out, not_9_out, not_10_out,
       not_11_out, not_12_out, not_13_out, not_14_out, not_15_out, not_16_out, not_17_out, not_18_out,
       not_19_out, not_20_out, not_21_out, not_22_out, not_23_out, not_24_out, not_25_out, not_26_out,
       not_27_out, not_28_out, not_29_out, not_30_out, not_31_out, not_32_out, not_33_out;
  wire [31:0] undriven;

  not not_1 (not_1_out, S);
  not not_2 (not_2_out, S);
  not not_3 (not_3_out, S);
  not not_4 (not_4_out, S);
  not not_5 (not_5_out, S);
  not not_6 (not_6_out, S);
  not not_7 (not_7_out, S);
  not not_8 (not_8_out, S);
  not not_9 (not_9_out, S);
  not not_10 (not_10_out, S);
  not not_11 (not_11_out, S);
  not not_12 (not_12_out, S);
  not not_13 (not_13_out, S);
  not not_14 (not_14_out, S);
  not not_15 (not_15_out, S);
  not not_16 (not_16_out, S);
  not not_17 (not_17_out, S);
  not not_18 (not_18_out, S);
  not not_19 (not_19_out, S);
  not not_20 (not_20_out, S);
  not not_21 (not_21_out, S);
  not not_22 (not_22_out, S);
  not not_23 (not_23_out, S);
  not not_24 (not_24_out, S);
  not not_25 (not_25_out, S);
  not not_26 (not_26_out, S);
  not not_27 (not_27_out, S);
  not not_28 (not_28_out, S);
  not not_29 (not_29_out, S);
  not not_30 (not_30_out, S);
  not not_31 (not_31_out, S);
  not not_32 (not_32_out, S);
  not not_33 (not_33_out, undriven[0]);
  and and_1 (and_1_out, not_1_out, undriven[31]);
  and and_2 (and_2_out, S, undriven[30]);
  and and_3 (and_3_out, not_2_out, undriven[30]);
  and and_4 (and_4_out, S, undriven[29]);
  and and_5 (and_5_out, not_3_out, undriven[29]);
  and and_6 (and_6_out, S, undriven[28]);
  and and_7 (and_7_out, not_4_out, undriven[28]);
  and and_8 (and_8_out, S, undriven[27]);
  and and_9 (and_9_out, not_5_out, undriven[27]);
  and and_10 (and_10_out, S, undriven[26]);
  and and_11 (and_11_out, not_6_out, undriven[26]);
  and and_12 (and_12_out, S, undriven[25]);
  and and_13 (and_13_out, not_7_out, undriven[25]);
  and and_14 (and_14_out, S, undriven[24]);
  and and_15 (and_15_out, not_8_out, undriven[24]);
  and and_16 (and_16_out, S, undriven[23]);
  and and_17 (and_17_out, not_9_out, undriven[23]);
  and and_18 (and_18_out, S, undriven[22]);
  and and_19 (and_19_out, not_10_out, undriven[22]);
  and and_20 (and_20_out, S, undriven[21]);
  and and_21 (and_21_out, not_11_out, undriven[21]);
  and and_22 (and_22_out, S, undriven[20]);
  and and_23 (and_23_out, not_12_out, undriven[20]);
  and and_24 (and_24_out, S, undriven[19]);
  and and_25 (and_25_out, not_13_out, undriven[19]);
  and and_26 (and_26_out, S, undriven[18]);
  and and_27 (and_27_out, not_14_out, undriven[18]);
  and and_28 (and_28_out, S, undriven[17]);
  and and_29 (and_29_out, not_15_out, undriven[17]);
  and and_30 (and_30_out, S, undriven[16]);
  and and_31 (and_31_out, not_16_out, undriven[16]);
  and and_32 (and_32_out, S, undriven[15]);
  and and_33 (and_33_out, not_17_out, undriven[15]);
  and and_34 (and_34_out, S, undriven[14]);
  and and_35 (and_35_out, not_18_out, undriven[14]);
  and and_36 (and_36_out, S, undriven[13]);
  and and_37 (and_37_out, not_19_out, undriven[13]);
  and and_38 (and_38_out, S, undriven[12]);
  and and_39 (and_39_out, not_20_out, undriven[12]);
  and and_40 (and_40_out, S, undriven[11]);
  and and_41 (and_41_out, not_21_out, undriven[11]);
  and and_42 (and_42_out, S, undriven[10]);
  and and_43 (and_43_out, not_22_out, undriven[10]);
  and and_44 (and_44_out, S, undriven[9]);
  and and_45 (and_45_out, not_23_out, undriven[9]);
  and and_46 (and_46_out, S, undriven[8]);
  and and_47 (and_47_out, not_24_out, undriven[8]);
  and and_48 (and_48_out, S, undriven[7]);
  and and_49 (and_49_out, not_25_out, undriven[7]);
  and and_50 (and_50_out, S, undriven[6]);
  and and_51 (and_51_out, not_26_out, undriven[6]);
  and and_52 (and_52_out, S, undriven[5]);
  and and_53 (and_53_out, not_27_out, undriven[5]);
  and and_54 (and_54_out, S, undriven[4]);
  and and_55 (and_55_out, not_28_out, undriven[4]);
  and and_56 (and_56_out, S, undriven[3]);
  and and_57 (and_57_out, not_29_out, undriven[3]);
  and and_58 (and_58_out, S, undriven[2]);
  and and_59 (and_59_out, not_30_out, undriven[2]);
  and and_60 (and_60_out, S, undriven[1]);
  and and_61 (and_61_out, not_31_out, undriven[1]);
  and and_62 (and_62_out, S, undriven[0]);
  and and_63 (and_63_out, not_32_out, undriven[0]);
  and and_64 (and_64_out, not_33_out, undriven[0]);
  // OR_Gate or_1 has open pins: in0=and_1_out, in1=and_2_out, out=open
  // OR_Gate or_2 has open pins: in0=and_3_out, in1=and_4_out, out=open
  // OR_Gate or_3 has open pins: in0=and_5_out, in1=and_6_out, out=open
  // OR_Gate or_4 has open pins: in0=and_7_out, in1=and_8_out, out=open
  // OR_Gate or_5 has open pins: in0=and_9_out, in1=and_10_out, out=open
  // OR_Gate or_6 has open pins: in0=and_11_out, in1=and_12_out, out=open
  // OR_Gate or_7 has open pins: in0=and_13_out, in1=and_14_out, out=open
  // OR_Gate or_8 has open pins: in0=and_15_out, in1=and_16_out, out=open
  // OR_Gate or_9 has open pins: in0=and_17_out, in1=and_18_out, out=open
  // OR_Gate or_10 has open pins: in0=and_19_out, in1=and_20_out, out=open
  // OR_Gate or_11 has open pins: in0=and_21_out, in1=and_22_out, out=open
  // OR_Gate or_12 has open pins: in0=and_23_out, in1=and_24_out, out=open
  // OR_Gate or_13 has open pins: in0=and_25_out, in1=and_26_out, out=open
  // OR_Gate or_14 has open pins: in0=and_27_out, in1=and_28_out, out=open
  // OR_Gate or_15 has open pins: in0=and_29_out, in1=and_30_out, out=open
  // OR_Gate or_16 has open pins: in0=and_31_out, in1=and_32_out, out=open
  // OR_Gate or_17 has open pins: in0=and_33_out, in1=and_34_out, out=open
  // OR_Gate or_18 has open pins: in0=and_35_out, in1=and_36_out, out=open
  // OR_Gate or_19 has open pins: in0=and_37_out, in1=and_38_out, out=open
  // OR_Gate or_20 has open pins: in0=and_39_out, in1=and_40_out, out=open
  // OR_Gate or_21 has open pins: in0=and_41_out, in1=and_42_out, out=open
  // OR_Gate or_22 has open pins: in0=and_43_out, in1=and_44_out, out=open
  // OR_Gate or_23 has open pins: in0=and_45_out, in1=and_46_out, out=open
  // OR_Gate or_24 has open pins: in0=and_47_out, in1=and_48_out, out=open
  // OR_Gate or_25 has open pins: in0=and_49_out, in1=and_50_out, out=open
  // OR_Gate or_26 has open pins: in0=and_51_out, in1=and_52_out, out=open
  // OR_Gate or_27 has open pins: in0=and_53_out, in1=and_54_out, out=open
  // OR_Gate or_28 has open pins: in0=and_55_out, in1=and_56_out, out=open
  // OR_Gate or_29 has open pins: in0=and_57_out, in1=and_58_out, out=open
  // OR_Gate or_30 has open pins: in0=and_59_out, in1=and_60_out, out=open
  // OR_Gate or_31 has open pins: in0=and_61_out, in1=and_62_out, out=open
  // OR_Gate or_32 has open pins: in0=and_63_out, in1=and_64_out, out=open
endmodule

module somador32bits (
  input  [31:0] A,
  input  [31:0] B,
  output [31:0] C
);

  wire fulladder_1_cout, fulladder_2_cout, fulladder_3_cout, fulladder_4_cout, fulladder_5_cout,
       fulladder_6_cout, fulladder_7_cout, fulladder_8_cout, fulladder_9_cout, fulladder_10_cout,
       fulladder_11_cout, fulladder_12_cout, fulladder_13_cout, fulladder_14_cout, fulladder_15_cout,
       fulladder_16_cout, fulladder_17_cout, fulladder_18_cout, fulladder_19_cout, fulladder_20_cout,
       fulladder_21_cout, fulladder_22_cout, fulladder_23_cout, fulladder_24_cout, fulladder_25_cout,
       fulladder_26_cout, fulladder_27_cout, fulladder_28_cout, fulladder_29_cout, fulladder_30_cout,
       halfadder_1_cout;

  HalfAdder halfadder_1 (.A0(A[0]), .B0(B[0]), .Cout(halfadder_1_cout), .S0(C[0]));
  FullAdder fulladder_1 (.Ax(A[1]), .Bx(B[1]), .Cin(halfadder_1_cout), .Sx(C[1]), .Cout(fulladder_1_cout));
  FullAdder fulladder_2 (.Ax(A[2]), .Bx(B[2]), .Cin(fulladder_1_cout), .Sx(C[2]), .Cout(fulladder_2_cout));
  FullAdder fulladder_3 (.Ax(A[3]), .Bx(B[3]), .Cin(fulladder_2_cout), .Sx(C[3]), .Cout(fulladder_3_cout));
  FullAdder fulladder_4 (.Ax(A[4]), .Bx(B[4]), .Cin(fulladder_3_cout), .Sx(C[4]), .Cout(fulladder_4_cout));
  FullAdder fulladder_5 (.Ax(A[5]), .Bx(B[5]), .Cin(fulladder_4_cout), .Sx(C[5]), .Cout(fulladder_5_cout));
  FullAdder fulladder_6 (.Ax(A[6]), .Bx(B[6]), .Cin(fulladder_5_cout), .Sx(C[6]), .Cout(fulladder_6_cout));
  FullAdder fulladder_7 (.Ax(A[7]), .Bx(B[7]), .Cin(fulladder_6_cout), .Sx(C[7]), .Cout(fulladder_7_cout));
  FullAdder fulladder_8 (.Ax(A[8]), .Bx(B[8]), .Cin(fulladder_7_cout), .Sx(C[8]), .Cout(fulladder_8_cout));
  FullAdder fulladder_9 (.Ax(A[9]), .Bx(B[9]), .Cin(fulladder_8_cout), .Sx(C[9]), .Cout(fulladder_9_cout));
  FullAdder fulladder_10 (.Ax(A[10]), .Bx(B[10]), .Cin(fulladder_9_cout), .Sx(C[10]), .Cout(fulladder_10_cout));
  FullAdder fulladder_11 (.Ax(A[11]), .Bx(B[11]), .Cin(fulladder_10_cout), .Sx(C[11]), .Cout(fulladder_11_cout));
  FullAdder fulladder_12 (.Ax(A[12]), .Bx(B[12]), .Cin(fulladder_11_cout), .Sx(C[12]), .Cout(fulladder_12_cout));
  FullAdder fulladder_13 (.Ax(A[13]), .Bx(B[13]), .Cin(fulladder_12_cout), .Sx(C[13]), .Cout(fulladder_13_cout));
  FullAdder fulladder_14 (.Ax(A[14]), .Bx(B[14]), .Cin(fulladder_13_cout), .Sx(C[14]), .Cout(fulladder_14_cout));
  FullAdder fulladder_15 (.Ax(A[15]), .Bx(B[15]), .Cin(fulladder_14_cout), .Sx(C[15]), .Cout(fulladder_15_cout));
  FullAdder fulladder_16 (.Ax(A[16]), .Bx(B[16]), .Cin(fulladder_15_cout), .Sx(C[16]), .Cout(fulladder_16_cout));
  FullAdder fulladder_17 (.Ax(A[17]), .Bx(B[17]), .Cin(fulladder_16_cout), .Sx(C[17]), .Cout(fulladder_17_cout));
  FullAdder fulladder_18 (.Ax(A[18]), .Bx(B[18]), .Cin(fulladder_17_cout), .Sx(C[18]), .Cout(fulladder_18_cout));
  FullAdder fulladder_19 (.Ax(A[19]), .Bx(B[19]), .Cin(fulladder_18_cout), .Sx(C[19]), .Cout(fulladder_19_cout));
  FullAdder fulladder_20 (.Ax(A[20]), .Bx(B[20]), .Cin(fulladder_19_cout), .Sx(C[20]), .Cout(fulladder_20_cout));
  FullAdder fulladder_21 (.Ax(A[21]), .Bx(B[21]), .Cin(fulladder_20_cout), .Sx(C[21]), .Cout(fulladder_21_cout));
  FullAdder fulladder_22 (.Ax(A[22]), .Bx(B[22]), .Cin(fulladder_21_cout), .Sx(C[22]), .Cout(fulladder_22_cout));
  FullAdder fulladder_23 (.Ax(A[23]), .Bx(B[23]), .Cin(fulladder_22_cout), .Sx(C[23]), .Cout(fulladder_23_cout));
  FullAdder fulladder_24 (.Ax(A[24]), .Bx(B[24]), .Cin(fulladder_23_cout), .Sx(C[24]), .Cout(fulladder_24_cout));
  FullAdder fulladder_25 (.Ax(A[25]), .Bx(B[25]), .Cin(fulladder_24_cout), .Sx(C[25]), .Cout(fulladder_25_cout));
  FullAdder fulladder_26 (.Ax(A[26]), .Bx(B[26]), .Cin(fulladder_25_cout), .Sx(C[26]), .Cout(fulladder_26_cout));
  FullAdder fulladder_27 (.Ax(A[27]), .Bx(B[27]), .Cin(fulladder_26_cout), .Sx(C[27]), .Cout(fulladder_27_cout));
  FullAdder fulladder_28 (.Ax(A[28]), .Bx(B[28]), .Cin(fulladder_27_cout), .Sx(C[28]), .Cout(fulladder_28_cout));
  FullAdder fulladder_29 (.Ax(A[29]), .Bx(B[29]), .Cin(fulladder_28_cout), .Sx(C[29]), .Cout(fulladder_29_cout));
  FullAdder fulladder_30 (.Ax(A[30]), .Bx(B[30]), .Cin(fulladder_29_cout), .Sx(C[30]), .Cout(fulladder_30_cout));
  FullAdder fulladder_31 (.Ax(A[31]), .Bx(B[31]), .Cin(fulladder_30_cout), .Sx(C[31]));  // open: Cout

  // Other names for the same wires on the sheet: num15 = B[16]; num16 = B[17]; num17 = B[18]
endmodule

module BancoRegistrador32bits (
  input  [31:0] C,
  input  Reiniciar,
  input  [3:0] endA,
  input  W,
  input  [3:0] endC,
  input  Clock,
  input  [3:0] endB,
  output [31:0] A,
  output [31:0] B
);

  wire multiplexer_2_out, multiplexer_3_out, multiplexer_4_out, multiplexer_5_out, multiplexer_6_out,
       multiplexer_7_out, multiplexer_8_out, multiplexer_9_out, multiplexer_10_out, multiplexer_11_out,
       multiplexer_12_out, multiplexer_13_out, multiplexer_14_out, multiplexer_15_out, multiplexer_16_out,
       W0, W1, W2, W3, W4, W5, W6, W7, W8, W9, W10, W11, W12, W13, W14, W15;
  wire [31:0] C_t, Q0, Q1, Q2, Q3, Q4, Q5, Q6, Q7, Q8, Q9, Q10, Q11, Q12, Q13, Q14, Q15;

  Demultiplexer #(.select(4)) demultiplexer_1 (
    .out0(W0), .out1(W1), .out2(W2), .out3(W3), .out4(W4), .out5(W5), .out6(W6), .out7(W7), .out8(W8),
    .out9(W9), .out10(W10), .out11(W11), .out12(W12), .out13(W13), .out14(W14), .out15(W15), .in(W),
    .sel(endC));
  Multiplexer #(.width(32)) multiplexer_1 (.in0(C), .in1({32{1'b0}}), .out(C_t), .sel(Reiniciar));
  Multiplexer multiplexer_2 (.in0(W1), .in1(1'b1), .out(multiplexer_2_out), .sel(Reiniciar));
  Multiplexer multiplexer_3 (.in0(W2), .in1(1'b1), .out(multiplexer_3_out), .sel(Reiniciar));
  Multiplexer multiplexer_4 (.in0(W3), .in1(1'b1), .out(multiplexer_4_out), .sel(Reiniciar));
  Multiplexer multiplexer_5 (.in0(W4), .in1(1'b1), .out(multiplexer_5_out), .sel(Reiniciar));
  Multiplexer multiplexer_6 (.in0(W5), .in1(1'b1), .out(multiplexer_6_out), .sel(Reiniciar));
  Multiplexer multiplexer_7 (.in0(W6), .in1(1'b1), .out(multiplexer_7_out), .sel(Reiniciar));
  Multiplexer multiplexer_8 (.in0(W7), .in1(1'b1), .out(multiplexer_8_out), .sel(Reiniciar));
  Multiplexer multiplexer_9 (.in0(W8), .in1(1'b1), .out(multiplexer_9_out), .sel(Reiniciar));
  Multiplexer multiplexer_10 (.in0(W9), .in1(1'b1), .out(multiplexer_10_out), .sel(Reiniciar));
  Multiplexer multiplexer_11 (.in0(W10), .in1(1'b1), .out(multiplexer_11_out), .sel(Reiniciar));
  Multiplexer multiplexer_12 (.in0(W11), .in1(1'b1), .out(multiplexer_12_out), .sel(Reiniciar));
  Multiplexer multiplexer_13 (.in0(W12), .in1(1'b1), .out(multiplexer_13_out), .sel(Reiniciar));
  Multiplexer multiplexer_14 (.in0(W13), .in1(1'b1), .out(multiplexer_14_out), .sel(Reiniciar));
  Multiplexer multiplexer_15 (.in0(W14), .in1(1'b1), .out(multiplexer_15_out), .sel(Reiniciar));
  Multiplexer multiplexer_16 (.in0(W15), .in1(1'b1), .out(multiplexer_16_out), .sel(Reiniciar));
  registrador32 registrador32_1 (.Dado({32{1'b0}}), .CLock(Clock), .Seletor(1'b1), .Q(Q0));
  registrador32 registrador32_2 (.Dado(C_t), .CLock(Clock), .Seletor(multiplexer_2_out), .Q(Q1));
  registrador32 registrador32_3 (.Dado(C_t), .CLock(Clock), .Seletor(multiplexer_3_out), .Q(Q2));
  registrador32 registrador32_4 (.Dado(C_t), .CLock(Clock), .Seletor(multiplexer_4_out), .Q(Q3));
  registrador32 registrador32_5 (.Dado(C_t), .CLock(Clock), .Seletor(multiplexer_5_out), .Q(Q4));
  registrador32 registrador32_6 (.Dado(C_t), .CLock(Clock), .Seletor(multiplexer_6_out), .Q(Q5));
  registrador32 registrador32_7 (.Dado(C_t), .CLock(Clock), .Seletor(multiplexer_7_out), .Q(Q6));
  registrador32 registrador32_8 (.Dado(C_t), .CLock(Clock), .Seletor(multiplexer_8_out), .Q(Q7));
  registrador32 registrador32_9 (.Dado(C_t), .CLock(Clock), .Seletor(multiplexer_9_out), .Q(Q8));
  registrador32 registrador32_10 (.Dado(C_t), .CLock(Clock), .Seletor(multiplexer_10_out), .Q(Q9));
  registrador32 registrador32_11 (.Dado(C_t), .CLock(Clock), .Seletor(multiplexer_11_out), .Q(Q10));
  registrador32 registrador32_12 (.Dado(C_t), .CLock(Clock), .Seletor(multiplexer_12_out), .Q(Q11));
  registrador32 registrador32_13 (.Dado(C_t), .CLock(Clock), .Seletor(multiplexer_13_out), .Q(Q12));
  registrador32 registrador32_14 (.Dado(C_t), .CLock(Clock), .Seletor(multiplexer_14_out), .Q(Q13));
  registrador32 registrador32_15 (.Dado(C_t), .CLock(Clock), .Seletor(multiplexer_15_out), .Q(Q14));
  registrador32 registrador32_16 (.Dado(C_t), .CLock(Clock), .Seletor(multiplexer_16_out), .Q(Q15));
  Multiplexer #(.select(4), .width(32)) multiplexer_17 (
    .in0(Q0), .in1(Q1), .in2(Q2), .in3(Q3), .in4(Q4), .in5(Q5), .in6(Q6), .in7(Q7), .in8(Q8), .in9(Q9),
    .in10(Q10), .in11(Q11), .in12(Q12), .in13(Q13), .in14(Q14), .in15(Q15), .out(A), .sel(endA));
  Multiplexer #(.select(4), .width(32)) multiplexer_18 (
    .in0(Q0), .in1(Q1), .in2(Q2), .in3(Q3), .in4(Q4), .in5(Q5), .in6(Q6), .in7(Q7), .in8(Q8), .in9(Q9),
    .in10(Q10), .in11(Q11), .in12(Q12), .in13(Q13), .in14(Q14), .in15(Q15), .out(B), .sel(endB));

  // Other names for the same wires on the sheet: Clk = Clock
endmodule

module subtrador32 (
  input  [31:0] A,
  input  [31:0] B,
  output [31:0] C
);

  wire [31:0] compldois32bitsv2_1_out_2;

  ComplDois32bitsV2 compldois32bitsv2_1 (.in_1(B), .out_2(compldois32bitsv2_1_out_2));
  somador32bits somador32bits_1 (.A(A), .B(compldois32bitsv2_1_out_2), .C(C));
endmodule

module ULA (
  input  [31:0] B,
  input  [31:0] A,
  input  [2:0] Funct,
  output out_4,
  output [31:0] C
);

  wire [31:0] and_1_out, multiplier_1_out, or_1_out, shiftter_1_c, somador32bits_1_c, subtrador32_1_c,
       xor_1_out;

  Multiplier #(.width(32)) multiplier_1 (.a(A), .b(B), .out(multiplier_1_out));  // open: cin, cout
  assign and_1_out = A & B;  // AND_Gate and_1, 32 bits wide
  assign or_1_out = A | B;  // OR_Gate or_1, 32 bits wide
  assign xor_1_out = A ^ B;  // XOR_Gate xor_1, 32 bits wide
  somador32bits somador32bits_1 (.A(A), .B(B), .C(somador32bits_1_c));
  subtrador32 subtrador32_1 (.A(A), .B(B), .C(subtrador32_1_c));
  shiftter shiftter_1 (.A(A), .B(B), .C(shiftter_1_c));
  Multiplexer #(.select(3), .width(32)) multiplexer_1 (
    .in0(somador32bits_1_c), .in1(subtrador32_1_c), .in2(multiplier_1_out), .in3(and_1_out), .in4(or_1_out),
    .in5(xor_1_out), .in6(shiftter_1_c), .out(C), .sel(Funct));  // open: in7
  detectorZero detectorzero_1 (.Q(C), .Zer0(out_4));
endmodule

module shift1 (
  input  [31:0] D,
  input  en,
  output [31:0] Q
);

  Multiplexer multiplexer_1 (.in0(D[31]), .in1(D[30]), .out(Q[31]), .sel(en));
  Multiplexer multiplexer_2 (.in0(D[30]), .in1(D[29]), .out(Q[30]), .sel(en));
  Multiplexer multiplexer_3 (.in0(D[29]), .in1(D[28]), .out(Q[29]), .sel(en));
  Multiplexer multiplexer_4 (.in0(D[28]), .in1(D[27]), .out(Q[28]), .sel(en));
  Multiplexer multiplexer_5 (.in0(D[27]), .in1(D[26]), .out(Q[27]), .sel(en));
  Multiplexer multiplexer_6 (.in0(D[26]), .in1(D[25]), .out(Q[26]), .sel(en));
  Multiplexer multiplexer_7 (.in0(D[25]), .in1(D[24]), .out(Q[25]), .sel(en));
  Multiplexer multiplexer_8 (.in0(D[24]), .in1(D[23]), .out(Q[24]), .sel(en));
  Multiplexer multiplexer_9 (.in0(D[23]), .in1(D[22]), .out(Q[23]), .sel(en));
  Multiplexer multiplexer_10 (.in0(D[22]), .in1(D[21]), .out(Q[22]), .sel(en));
  Multiplexer multiplexer_11 (.in0(D[21]), .in1(D[20]), .out(Q[21]), .sel(en));
  Multiplexer multiplexer_12 (.in0(D[20]), .in1(D[19]), .out(Q[20]), .sel(en));
  Multiplexer multiplexer_13 (.in0(D[19]), .in1(D[18]), .out(Q[19]), .sel(en));
  Multiplexer multiplexer_14 (.in0(D[18]), .in1(D[17]), .out(Q[18]), .sel(en));
  Multiplexer multiplexer_15 (.in0(D[17]), .in1(D[16]), .out(Q[17]), .sel(en));
  Multiplexer multiplexer_16 (.in0(D[16]), .in1(D[15]), .out(Q[16]), .sel(en));
  Multiplexer multiplexer_17 (.in0(D[15]), .in1(D[14]), .out(Q[15]), .sel(en));
  Multiplexer multiplexer_18 (.in0(D[14]), .in1(D[13]), .out(Q[14]), .sel(en));
  Multiplexer multiplexer_19 (.in0(D[13]), .in1(D[12]), .out(Q[13]), .sel(en));
  Multiplexer multiplexer_20 (.in0(D[12]), .in1(D[11]), .out(Q[12]), .sel(en));
  Multiplexer multiplexer_21 (.in0(D[11]), .in1(D[10]), .out(Q[11]), .sel(en));
  Multiplexer multiplexer_22 (.in0(D[10]), .in1(D[9]), .out(Q[10]), .sel(en));
  Multiplexer multiplexer_23 (.in0(D[9]), .in1(D[8]), .out(Q[9]), .sel(en));
  Multiplexer multiplexer_24 (.in0(D[8]), .in1(D[7]), .out(Q[8]), .sel(en));
  Multiplexer multiplexer_25 (.in0(D[7]), .in1(D[6]), .out(Q[7]), .sel(en));
  Multiplexer multiplexer_26 (.in0(D[6]), .in1(D[5]), .out(Q[6]), .sel(en));
  Multiplexer multiplexer_27 (.in0(D[5]), .in1(D[4]), .out(Q[5]), .sel(en));
  Multiplexer multiplexer_28 (.in0(D[4]), .in1(D[3]), .out(Q[4]), .sel(en));
  Multiplexer multiplexer_29 (.in0(D[3]), .in1(D[2]), .out(Q[3]), .sel(en));
  Multiplexer multiplexer_30 (.in0(D[2]), .in1(D[1]), .out(Q[2]), .sel(en));
  Multiplexer multiplexer_31 (.in0(D[1]), .in1(D[0]), .out(Q[1]), .sel(en));
  Multiplexer multiplexer_32 (.in0(D[0]), .in1(1'b0), .out(Q[0]), .sel(en));
endmodule

module shift2 (
  input  [31:0] D,
  input  En,
  output [31:0] Q
);

  Multiplexer multiplexer_1 (.in0(D[31]), .in1(D[29]), .out(Q[31]), .sel(En));
  Multiplexer multiplexer_2 (.in0(D[30]), .in1(D[28]), .out(Q[30]), .sel(En));
  Multiplexer multiplexer_3 (.in0(D[29]), .in1(D[27]), .out(Q[29]), .sel(En));
  Multiplexer multiplexer_4 (.in0(D[28]), .in1(D[26]), .out(Q[28]), .sel(En));
  Multiplexer multiplexer_5 (.in0(D[27]), .in1(D[25]), .out(Q[27]), .sel(En));
  Multiplexer multiplexer_6 (.in0(D[26]), .in1(D[24]), .out(Q[26]), .sel(En));
  Multiplexer multiplexer_7 (.in0(D[25]), .in1(D[23]), .out(Q[25]), .sel(En));
  Multiplexer multiplexer_8 (.in0(D[24]), .in1(D[22]), .out(Q[24]), .sel(En));
  Multiplexer multiplexer_9 (.in0(D[23]), .in1(D[21]), .out(Q[23]), .sel(En));
  Multiplexer multiplexer_10 (.in0(D[22]), .in1(D[20]), .out(Q[22]), .sel(En));
  Multiplexer multiplexer_11 (.in0(D[21]), .in1(D[19]), .out(Q[21]), .sel(En));
  Multiplexer multiplexer_12 (.in0(D[20]), .in1(D[18]), .out(Q[20]), .sel(En));
  Multiplexer multiplexer_13 (.in0(D[19]), .in1(D[17]), .out(Q[19]), .sel(En));
  Multiplexer multiplexer_14 (.in0(D[18]), .in1(D[16]), .out(Q[18]), .sel(En));
  Multiplexer multiplexer_15 (.in0(D[17]), .in1(D[15]), .out(Q[17]), .sel(En));
  Multiplexer multiplexer_16 (.in0(D[16]), .in1(D[14]), .out(Q[16]), .sel(En));
  Multiplexer multiplexer_17 (.in0(D[15]), .in1(D[13]), .out(Q[15]), .sel(En));
  Multiplexer multiplexer_18 (.in0(D[14]), .in1(D[12]), .out(Q[14]), .sel(En));
  Multiplexer multiplexer_19 (.in0(D[13]), .in1(D[11]), .out(Q[13]), .sel(En));
  Multiplexer multiplexer_20 (.in0(D[12]), .in1(D[10]), .out(Q[12]), .sel(En));
  Multiplexer multiplexer_21 (.in0(D[11]), .in1(D[9]), .out(Q[11]), .sel(En));
  Multiplexer multiplexer_22 (.in0(D[10]), .in1(D[8]), .out(Q[10]), .sel(En));
  Multiplexer multiplexer_23 (.in0(D[9]), .in1(D[7]), .out(Q[9]), .sel(En));
  Multiplexer multiplexer_24 (.in0(D[8]), .in1(D[6]), .out(Q[8]), .sel(En));
  Multiplexer multiplexer_25 (.in0(D[7]), .in1(D[5]), .out(Q[7]), .sel(En));
  Multiplexer multiplexer_26 (.in0(D[6]), .in1(D[4]), .out(Q[6]), .sel(En));
  Multiplexer multiplexer_27 (.in0(D[5]), .in1(D[3]), .out(Q[5]), .sel(En));
  Multiplexer multiplexer_28 (.in0(D[4]), .in1(D[2]), .out(Q[4]), .sel(En));
  Multiplexer multiplexer_29 (.in0(D[3]), .in1(D[1]), .out(Q[3]), .sel(En));
  Multiplexer multiplexer_30 (.in0(D[2]), .in1(D[0]), .out(Q[2]), .sel(En));
  Multiplexer multiplexer_31 (.in0(D[1]), .in1(1'b0), .out(Q[1]), .sel(En));
  Multiplexer multiplexer_32 (.in0(D[0]), .in1(1'b0), .out(Q[0]), .sel(En));
endmodule

module shift4 (
  input  [31:0] D,
  input  En,
  output [31:0] Q
);

  Multiplexer multiplexer_1 (.in0(D[31]), .in1(D[27]), .out(Q[31]), .sel(En));
  Multiplexer multiplexer_2 (.in0(D[30]), .in1(D[26]), .out(Q[30]), .sel(En));
  Multiplexer multiplexer_3 (.in0(D[29]), .in1(D[25]), .out(Q[29]), .sel(En));
  Multiplexer multiplexer_4 (.in0(D[28]), .in1(D[24]), .out(Q[28]), .sel(En));
  Multiplexer multiplexer_5 (.in0(D[27]), .in1(D[23]), .out(Q[27]), .sel(En));
  Multiplexer multiplexer_6 (.in0(D[26]), .in1(D[22]), .out(Q[26]), .sel(En));
  Multiplexer multiplexer_7 (.in0(D[25]), .in1(D[21]), .out(Q[25]), .sel(En));
  Multiplexer multiplexer_8 (.in0(D[24]), .in1(D[20]), .out(Q[24]), .sel(En));
  Multiplexer multiplexer_9 (.in0(D[23]), .in1(D[19]), .out(Q[23]), .sel(En));
  Multiplexer multiplexer_10 (.in0(D[22]), .in1(D[18]), .out(Q[22]), .sel(En));
  Multiplexer multiplexer_11 (.in0(D[21]), .in1(D[17]), .out(Q[21]), .sel(En));
  Multiplexer multiplexer_12 (.in0(D[20]), .in1(D[16]), .out(Q[20]), .sel(En));
  Multiplexer multiplexer_13 (.in0(D[19]), .in1(D[15]), .out(Q[19]), .sel(En));
  Multiplexer multiplexer_14 (.in0(D[18]), .in1(D[14]), .out(Q[18]), .sel(En));
  Multiplexer multiplexer_15 (.in0(D[17]), .in1(D[13]), .out(Q[17]), .sel(En));
  Multiplexer multiplexer_16 (.in0(D[16]), .in1(D[12]), .out(Q[16]), .sel(En));
  Multiplexer multiplexer_17 (.in0(D[15]), .in1(D[11]), .out(Q[15]), .sel(En));
  Multiplexer multiplexer_18 (.in0(D[14]), .in1(D[10]), .out(Q[14]), .sel(En));
  Multiplexer multiplexer_19 (.in0(D[13]), .in1(D[9]), .out(Q[13]), .sel(En));
  Multiplexer multiplexer_20 (.in0(D[12]), .in1(D[8]), .out(Q[12]), .sel(En));
  Multiplexer multiplexer_21 (.in0(D[11]), .in1(D[7]), .out(Q[11]), .sel(En));
  Multiplexer multiplexer_22 (.in0(D[10]), .in1(D[6]), .out(Q[10]), .sel(En));
  Multiplexer multiplexer_23 (.in0(D[9]), .in1(D[5]), .out(Q[9]), .sel(En));
  Multiplexer multiplexer_24 (.in0(D[8]), .in1(D[4]), .out(Q[8]), .sel(En));
  Multiplexer multiplexer_25 (.in0(D[7]), .in1(D[3]), .out(Q[7]), .sel(En));
  Multiplexer multiplexer_26 (.in0(D[6]), .in1(D[2]), .out(Q[6]), .sel(En));
  Multiplexer multiplexer_27 (.in0(D[5]), .in1(D[1]), .out(Q[5]), .sel(En));
  Multiplexer multiplexer_28 (.in0(D[4]), .in1(D[0]), .out(Q[4]), .sel(En));
  Multiplexer multiplexer_29 (.in0(D[3]), .in1(1'b0), .out(Q[3]), .sel(En));
  Multiplexer multiplexer_30 (.in0(D[2]), .in1(1'b0), .out(Q[2]), .sel(En));
  Multiplexer multiplexer_31 (.in0(D[1]), .in1(1'b0), .out(Q[1]), .sel(En));
  Multiplexer multiplexer_32 (.in0(D[0]), .in1(1'b0), .out(Q[0]), .sel(En));
endmodule

module shift8 (
  input  [31:0] D,
  input  En,
  output [31:0] Q
);

  Multiplexer multiplexer_1 (.in0(D[31]), .in1(D[23]), .out(Q[31]), .sel(En));
  Multiplexer multiplexer_2 (.in0(D[30]), .in1(D[22]), .out(Q[30]), .sel(En));
  Multiplexer multiplexer_3 (.in0(D[29]), .in1(D[21]), .out(Q[29]), .sel(En));
  Multiplexer multiplexer_4 (.in0(D[28]), .in1(D[20]), .out(Q[28]), .sel(En));
  Multiplexer multiplexer_5 (.in0(D[27]), .in1(D[19]), .out(Q[27]), .sel(En));
  Multiplexer multiplexer_6 (.in0(D[26]), .in1(D[18]), .out(Q[26]), .sel(En));
  Multiplexer multiplexer_7 (.in0(D[25]), .in1(D[17]), .out(Q[25]), .sel(En));
  Multiplexer multiplexer_8 (.in0(D[24]), .in1(D[16]), .out(Q[24]), .sel(En));
  Multiplexer multiplexer_9 (.in0(D[23]), .in1(D[15]), .out(Q[23]), .sel(En));
  Multiplexer multiplexer_10 (.in0(D[22]), .in1(D[14]), .out(Q[22]), .sel(En));
  Multiplexer multiplexer_11 (.in0(D[21]), .in1(D[13]), .out(Q[21]), .sel(En));
  Multiplexer multiplexer_12 (.in0(D[20]), .in1(D[12]), .out(Q[20]), .sel(En));
  Multiplexer multiplexer_13 (.in0(D[19]), .in1(D[11]), .out(Q[19]), .sel(En));
  Multiplexer multiplexer_14 (.in0(D[18]), .in1(D[10]), .out(Q[18]), .sel(En));
  Multiplexer multiplexer_15 (.in0(D[17]), .in1(D[9]), .out(Q[17]), .sel(En));
  Multiplexer multiplexer_16 (.in0(D[16]), .in1(D[8]), .out(Q[16]), .sel(En));
  Multiplexer multiplexer_17 (.in0(D[15]), .in1(D[7]), .out(Q[15]), .sel(En));
  Multiplexer multiplexer_18 (.in0(D[14]), .in1(D[6]), .out(Q[14]), .sel(En));
  Multiplexer multiplexer_19 (.in0(D[13]), .in1(D[5]), .out(Q[13]), .sel(En));
  Multiplexer multiplexer_20 (.in0(D[12]), .in1(D[4]), .out(Q[12]), .sel(En));
  Multiplexer multiplexer_21 (.in0(D[11]), .in1(D[3]), .out(Q[11]), .sel(En));
  Multiplexer multiplexer_22 (.in0(D[10]), .in1(D[2]), .out(Q[10]), .sel(En));
  Multiplexer multiplexer_23 (.in0(D[9]), .in1(D[1]), .out(Q[9]), .sel(En));
  Multiplexer multiplexer_24 (.in0(D[8]), .in1(D[0]), .out(Q[8]), .sel(En));
  Multiplexer multiplexer_25 (.in0(D[7]), .in1(1'b0), .out(Q[7]), .sel(En));
  Multiplexer multiplexer_26 (.in0(D[6]), .in1(1'b0), .out(Q[6]), .sel(En));
  Multiplexer multiplexer_27 (.in0(D[5]), .in1(1'b0), .out(Q[5]), .sel(En));
  Multiplexer multiplexer_28 (.in0(D[4]), .in1(1'b0), .out(Q[4]), .sel(En));
  Multiplexer multiplexer_29 (.in0(D[3]), .in1(1'b0), .out(Q[3]), .sel(En));
  Multiplexer multiplexer_30 (.in0(D[2]), .in1(1'b0), .out(Q[2]), .sel(En));
  Multiplexer multiplexer_31 (.in0(D[1]), .in1(1'b0), .out(Q[1]), .sel(En));
  Multiplexer multiplexer_32 (.in0(D[0]), .in1(1'b0), .out(Q[0]), .sel(En));
endmodule

module shift16 (
  input  [31:0] D,
  input  En,
  output [31:0] Q
);

  Multiplexer multiplexer_1 (.in0(D[31]), .in1(D[15]), .out(Q[31]), .sel(En));
  Multiplexer multiplexer_2 (.in0(D[30]), .in1(D[14]), .out(Q[30]), .sel(En));
  Multiplexer multiplexer_3 (.in0(D[29]), .in1(D[13]), .out(Q[29]), .sel(En));
  Multiplexer multiplexer_4 (.in0(D[28]), .in1(D[12]), .out(Q[28]), .sel(En));
  Multiplexer multiplexer_5 (.in0(D[27]), .in1(D[11]), .out(Q[27]), .sel(En));
  Multiplexer multiplexer_6 (.in0(D[26]), .in1(D[10]), .out(Q[26]), .sel(En));
  Multiplexer multiplexer_7 (.in0(D[25]), .in1(D[9]), .out(Q[25]), .sel(En));
  Multiplexer multiplexer_8 (.in0(D[24]), .in1(D[8]), .out(Q[24]), .sel(En));
  Multiplexer multiplexer_9 (.in0(D[23]), .in1(D[7]), .out(Q[23]), .sel(En));
  Multiplexer multiplexer_10 (.in0(D[22]), .in1(D[6]), .out(Q[22]), .sel(En));
  Multiplexer multiplexer_11 (.in0(D[21]), .in1(D[5]), .out(Q[21]), .sel(En));
  Multiplexer multiplexer_12 (.in0(D[20]), .in1(D[4]), .out(Q[20]), .sel(En));
  Multiplexer multiplexer_13 (.in0(D[19]), .in1(D[3]), .out(Q[19]), .sel(En));
  Multiplexer multiplexer_14 (.in0(D[18]), .in1(D[2]), .out(Q[18]), .sel(En));
  Multiplexer multiplexer_15 (.in0(D[17]), .in1(D[1]), .out(Q[17]), .sel(En));
  Multiplexer multiplexer_16 (.in0(D[16]), .in1(D[0]), .out(Q[16]), .sel(En));
  Multiplexer multiplexer_17 (.in0(D[15]), .in1(1'b0), .out(Q[15]), .sel(En));
  Multiplexer multiplexer_18 (.in0(D[14]), .in1(1'b0), .out(Q[14]), .sel(En));
  Multiplexer multiplexer_19 (.in0(D[13]), .in1(1'b0), .out(Q[13]), .sel(En));
  Multiplexer multiplexer_20 (.in0(D[12]), .in1(1'b0), .out(Q[12]), .sel(En));
  Multiplexer multiplexer_21 (.in0(D[11]), .in1(1'b0), .out(Q[11]), .sel(En));
  Multiplexer multiplexer_22 (.in0(D[10]), .in1(1'b0), .out(Q[10]), .sel(En));
  Multiplexer multiplexer_23 (.in0(D[9]), .in1(1'b0), .out(Q[9]), .sel(En));
  Multiplexer multiplexer_24 (.in0(D[8]), .in1(1'b0), .out(Q[8]), .sel(En));
  Multiplexer multiplexer_25 (.in0(D[7]), .in1(1'b0), .out(Q[7]), .sel(En));
  Multiplexer multiplexer_26 (.in0(D[6]), .in1(1'b0), .out(Q[6]), .sel(En));
  Multiplexer multiplexer_27 (.in0(D[5]), .in1(1'b0), .out(Q[5]), .sel(En));
  Multiplexer multiplexer_28 (.in0(D[4]), .in1(1'b0), .out(Q[4]), .sel(En));
  Multiplexer multiplexer_29 (.in0(D[3]), .in1(1'b0), .out(Q[3]), .sel(En));
  Multiplexer multiplexer_30 (.in0(D[2]), .in1(1'b0), .out(Q[2]), .sel(En));
  Multiplexer multiplexer_31 (.in0(D[1]), .in1(1'b0), .out(Q[1]), .sel(En));
  Multiplexer multiplexer_32 (.in0(D[0]), .in1(1'b0), .out(Q[0]), .sel(En));
endmodule

module shiftter (
  input  [31:0] A,
  input  [31:0] B,
  output [31:0] C
);

  wire detectorzero_1_zer0, not_1_out;
  wire [31:0] shift1_1_q, shift2_1_q, shift4_1_q, shift8_1_q, shift16_1_q;

  detectorZero detectorzero_1 (.Zer0(detectorzero_1_zer0));  // open: Q
  shift1 shift1_1 (.D(A), .en(B[0]), .Q(shift1_1_q));
  shift2 shift2_1 (.D(shift1_1_q), .En(B[1]), .Q(shift2_1_q));
  shift4 shift4_1 (.D(shift2_1_q), .En(B[2]), .Q(shift4_1_q));
  shift8 shift8_1 (.D(shift4_1_q), .En(B[3]), .Q(shift8_1_q));
  shift16 shift16_1 (.D(shift8_1_q), .En(B[4]), .Q(shift16_1_q));
  not not_1 (not_1_out, detectorzero_1_zer0);
  Multiplexer #(.width(32)) multiplexer_1 (.in0(shift16_1_q), .in1({32{1'b0}}), .out(C), .sel(not_1_out));
endmodule

module detectorZero (
  input  [31:0] Q,
  output Zer0
);

  nor nor_1 (Zer0, Q[31], Q[30], Q[29], Q[28], Q[27], Q[26], Q[25], Q[24], Q[23], Q[22], Q[21], Q[20], Q[19], Q[18], Q[17], Q[16], Q[15], Q[14], Q[13], Q[12], Q[11], Q[10], Q[9], Q[8], Q[7], Q[6], Q[5], Q[4], Q[3], Q[2], Q[1], Q[0]);
endmodule

module extZero (
  input  [15:0] Imed,
  output [31:0] S
);


  assign S = {{16{1'b0}}, Imed};
endmodule

module extSinal (
  input  [15:0] Imed,
  output [23:0] S
);


  assign S = {{9{Imed[15]}}, Imed[14:0]};
endmodule

module PC (
  input  [23:0] in_1,
  input  Reiniciar,
  input  Clock,
  input  Halt,
  output [23:0] out_5
);

  wire multiplexer_2_out, not_1_out;
  wire [23:0] multiplexer_1_out;

  Multiplexer #(.width(24)) multiplexer_1 (.in0(in_1), .in1({24{1'b0}}), .out(multiplexer_1_out), .sel(Reiniciar));
  Multiplexer multiplexer_2 (.in0(not_1_out), .in1(1'b1), .out(multiplexer_2_out), .sel(Reiniciar));
  not not_1 (not_1_out, Halt);
  registrador24 registrador24_1 (.Dado(multiplexer_1_out), .CLock(Clock), .W(multiplexer_2_out), .Q(out_5));
endmodule

module registrador24 (
  input  [23:0] Dado,
  input  CLock,
  input  W,
  output [23:0] Q
);

  wire multiplexer_1_out, multiplexer_2_out, multiplexer_3_out, multiplexer_4_out, multiplexer_5_out,
       multiplexer_6_out, multiplexer_7_out, multiplexer_8_out, multiplexer_9_out, multiplexer_10_out,
       multiplexer_11_out, multiplexer_12_out, multiplexer_13_out, multiplexer_14_out, multiplexer_15_out,
       multiplexer_16_out, multiplexer_17_out, multiplexer_18_out, multiplexer_19_out, multiplexer_20_out,
       multiplexer_21_out, multiplexer_22_out, multiplexer_23_out, multiplexer_24_out;

  Multiplexer multiplexer_1 (.in0(Q[0]), .in1(Dado[0]), .out(multiplexer_1_out), .sel(W));
  Multiplexer multiplexer_2 (.in0(Q[1]), .in1(Dado[1]), .out(multiplexer_2_out), .sel(W));
  Multiplexer multiplexer_3 (.in0(Q[2]), .in1(Dado[2]), .out(multiplexer_3_out), .sel(W));
  Multiplexer multiplexer_4 (.in0(Q[3]), .in1(Dado[3]), .out(multiplexer_4_out), .sel(W));
  Multiplexer multiplexer_5 (.in0(Q[4]), .in1(Dado[4]), .out(multiplexer_5_out), .sel(W));
  Multiplexer multiplexer_6 (.in0(Q[5]), .in1(Dado[5]), .out(multiplexer_6_out), .sel(W));
  Multiplexer multiplexer_7 (.in0(Q[6]), .in1(Dado[6]), .out(multiplexer_7_out), .sel(W));
  Multiplexer multiplexer_8 (.in0(Q[7]), .in1(Dado[7]), .out(multiplexer_8_out), .sel(W));
  Multiplexer multiplexer_9 (.in0(Q[8]), .in1(Dado[8]), .out(multiplexer_9_out), .sel(W));
  Multiplexer multiplexer_10 (.in0(Q[9]), .in1(Dado[9]), .out(multiplexer_10_out), .sel(W));
  Multiplexer multiplexer_11 (.in0(Q[10]), .in1(Dado[10]), .out(multiplexer_11_out), .sel(W));
  Multiplexer multiplexer_12 (.in0(Q[11]), .in1(Dado[11]), .out(multiplexer_12_out), .sel(W));
  Multiplexer multiplexer_13 (.in0(Q[12]), .in1(Dado[12]), .out(multiplexer_13_out), .sel(W));
  Multiplexer multiplexer_14 (.in0(Q[13]), .in1(Dado[13]), .out(multiplexer_14_out), .sel(W));
  Multiplexer multiplexer_15 (.in0(Q[14]), .in1(Dado[14]), .out(multiplexer_15_out), .sel(W));
  Multiplexer multiplexer_16 (.in0(Q[15]), .in1(Dado[15]), .out(multiplexer_16_out), .sel(W));
  Multiplexer multiplexer_17 (.in0(Q[16]), .in1(Dado[16]), .out(multiplexer_17_out), .sel(W));
  Multiplexer multiplexer_18 (.in0(Q[17]), .in1(Dado[17]), .out(multiplexer_18_out), .sel(W));
  Multiplexer multiplexer_19 (.in0(Q[18]), .in1(Dado[18]), .out(multiplexer_19_out), .sel(W));
  Multiplexer multiplexer_20 (.in0(Q[19]), .in1(Dado[19]), .out(multiplexer_20_out), .sel(W));
  Multiplexer multiplexer_21 (.in0(Q[20]), .in1(Dado[20]), .out(multiplexer_21_out), .sel(W));
  Multiplexer multiplexer_22 (.in0(Q[21]), .in1(Dado[21]), .out(multiplexer_22_out), .sel(W));
  Multiplexer multiplexer_23 (.in0(Q[22]), .in1(Dado[22]), .out(multiplexer_23_out), .sel(W));
  Multiplexer multiplexer_24 (.in0(Q[23]), .in1(Dado[23]), .out(multiplexer_24_out), .sel(W));
  flipflop32 FF0 (.Dado(multiplexer_1_out), .Enable(CLock), .Q(Q[0]));  // open: nQ
  flipflop32 FF1 (.Dado(multiplexer_2_out), .Enable(CLock), .Q(Q[1]));  // open: nQ
  flipflop32 FF2 (.Dado(multiplexer_3_out), .Enable(CLock), .Q(Q[2]));  // open: nQ
  flipflop32 FF3 (.Dado(multiplexer_4_out), .Enable(CLock), .Q(Q[3]));  // open: nQ
  flipflop32 FF4 (.Dado(multiplexer_5_out), .Enable(CLock), .Q(Q[4]));  // open: nQ
  flipflop32 FF5 (.Dado(multiplexer_6_out), .Enable(CLock), .Q(Q[5]));  // open: nQ
  flipflop32 FF6 (.Dado(multiplexer_7_out), .Enable(CLock), .Q(Q[6]));  // open: nQ
  flipflop32 FF7 (.Dado(multiplexer_8_out), .Enable(CLock), .Q(Q[7]));  // open: nQ
  flipflop32 FF8 (.Dado(multiplexer_9_out), .Enable(CLock), .Q(Q[8]));  // open: nQ
  flipflop32 FF9 (.Dado(multiplexer_10_out), .Enable(CLock), .Q(Q[9]));  // open: nQ
  flipflop32 FF10 (.Dado(multiplexer_11_out), .Enable(CLock), .Q(Q[10]));  // open: nQ
  flipflop32 FF11 (.Dado(multiplexer_12_out), .Enable(CLock), .Q(Q[11]));  // open: nQ
  flipflop32 FF12 (.Dado(multiplexer_13_out), .Enable(CLock), .Q(Q[12]));  // open: nQ
  flipflop32 FF13 (.Dado(multiplexer_14_out), .Enable(CLock), .Q(Q[13]));  // open: nQ
  flipflop32 FF14 (.Dado(multiplexer_15_out), .Enable(CLock), .Q(Q[14]));  // open: nQ
  flipflop32 FF15 (.Dado(multiplexer_16_out), .Enable(CLock), .Q(Q[15]));  // open: nQ
  flipflop32 FF16 (.Dado(multiplexer_17_out), .Enable(CLock), .Q(Q[16]));  // open: nQ
  flipflop32 FF17 (.Dado(multiplexer_18_out), .Enable(CLock), .Q(Q[17]));  // open: nQ
  flipflop32 FF18 (.Dado(multiplexer_19_out), .Enable(CLock), .Q(Q[18]));  // open: nQ
  flipflop32 FF19 (.Dado(multiplexer_20_out), .Enable(CLock), .Q(Q[19]));  // open: nQ
  flipflop32 FF22 (.Dado(multiplexer_23_out), .Enable(CLock), .Q(Q[22]));  // open: nQ
  flipflop32 FF23 (.Dado(multiplexer_24_out), .Enable(CLock), .Q(Q[23]));  // open: nQ
  flipflop32 FF20 (.Dado(multiplexer_21_out), .Enable(CLock), .Q(Q[20]));  // open: nQ
  flipflop32 FF21 (.Dado(multiplexer_22_out), .Enable(CLock), .Q(Q[21]));  // open: nQ

  // Other names for the same wires on the sheet: Clk = CLock
endmodule

module somador24bits (
  input  [23:0] B,
  input  [23:0] A,
  output [23:0] PC_4
);

  wire fulladder_1_cout, fulladder_2_cout, fulladder_3_cout, fulladder_4_cout, fulladder_5_cout,
       fulladder_6_cout, fulladder_7_cout, fulladder_8_cout, fulladder_9_cout, fulladder_10_cout,
       fulladder_11_cout, fulladder_12_cout, fulladder_13_cout, fulladder_14_cout, fulladder_15_cout,
       fulladder_16_cout, fulladder_17_cout, fulladder_18_cout, fulladder_19_cout, fulladder_20_cout,
       fulladder_21_cout, fulladder_22_cout, halfadder_1_cout;

  HalfAdder halfadder_1 (.A0(A[0]), .B0(B[0]), .Cout(halfadder_1_cout), .S0(PC_4[0]));
  FullAdder fulladder_1 (.Ax(A[1]), .Bx(B[1]), .Cin(halfadder_1_cout), .Sx(PC_4[1]), .Cout(fulladder_1_cout));
  FullAdder fulladder_2 (.Ax(A[2]), .Bx(B[2]), .Cin(fulladder_1_cout), .Sx(PC_4[2]), .Cout(fulladder_2_cout));
  FullAdder fulladder_3 (.Ax(A[3]), .Bx(B[3]), .Cin(fulladder_2_cout), .Sx(PC_4[3]), .Cout(fulladder_3_cout));
  FullAdder fulladder_4 (.Ax(A[4]), .Bx(B[4]), .Cin(fulladder_3_cout), .Sx(PC_4[4]), .Cout(fulladder_4_cout));
  FullAdder fulladder_5 (.Ax(A[5]), .Bx(B[5]), .Cin(fulladder_4_cout), .Sx(PC_4[5]), .Cout(fulladder_5_cout));
  FullAdder fulladder_6 (.Ax(A[6]), .Bx(B[6]), .Cin(fulladder_5_cout), .Sx(PC_4[6]), .Cout(fulladder_6_cout));
  FullAdder fulladder_7 (.Ax(A[7]), .Bx(B[7]), .Cin(fulladder_6_cout), .Sx(PC_4[7]), .Cout(fulladder_7_cout));
  FullAdder fulladder_8 (.Ax(A[8]), .Bx(B[8]), .Cin(fulladder_7_cout), .Sx(PC_4[8]), .Cout(fulladder_8_cout));
  FullAdder fulladder_9 (.Ax(A[9]), .Bx(B[9]), .Cin(fulladder_8_cout), .Sx(PC_4[9]), .Cout(fulladder_9_cout));
  FullAdder fulladder_10 (.Ax(A[10]), .Bx(B[10]), .Cin(fulladder_9_cout), .Sx(PC_4[10]), .Cout(fulladder_10_cout));
  FullAdder fulladder_11 (.Ax(A[11]), .Bx(B[11]), .Cin(fulladder_10_cout), .Sx(PC_4[11]), .Cout(fulladder_11_cout));
  FullAdder fulladder_12 (.Ax(A[12]), .Bx(B[12]), .Cin(fulladder_11_cout), .Sx(PC_4[12]), .Cout(fulladder_12_cout));
  FullAdder fulladder_13 (.Ax(A[13]), .Bx(B[13]), .Cin(fulladder_12_cout), .Sx(PC_4[13]), .Cout(fulladder_13_cout));
  FullAdder fulladder_14 (.Ax(A[14]), .Bx(B[14]), .Cin(fulladder_13_cout), .Sx(PC_4[14]), .Cout(fulladder_14_cout));
  FullAdder fulladder_15 (.Ax(A[15]), .Bx(B[15]), .Cin(fulladder_14_cout), .Sx(PC_4[15]), .Cout(fulladder_15_cout));
  FullAdder fulladder_16 (.Ax(A[16]), .Bx(B[16]), .Cin(fulladder_15_cout), .Sx(PC_4[16]), .Cout(fulladder_16_cout));
  FullAdder fulladder_17 (.Ax(A[17]), .Bx(B[17]), .Cin(fulladder_16_cout), .Sx(PC_4[17]), .Cout(fulladder_17_cout));
  FullAdder fulladder_18 (.Ax(A[18]), .Bx(B[18]), .Cin(fulladder_17_cout), .Sx(PC_4[18]), .Cout(fulladder_18_cout));
  FullAdder fulladder_19 (.Ax(A[19]), .Bx(B[19]), .Cin(fulladder_18_cout), .Sx(PC_4[19]), .Cout(fulladder_19_cout));
  FullAdder fulladder_20 (.Ax(A[20]), .Bx(B[20]), .Cin(fulladder_19_cout), .Sx(PC_4[20]), .Cout(fulladder_20_cout));
  FullAdder fulladder_21 (.Ax(A[21]), .Bx(B[21]), .Cin(fulladder_20_cout), .Sx(PC_4[21]), .Cout(fulladder_21_cout));
  FullAdder fulladder_22 (.Ax(A[22]), .Bx(B[22]), .Cin(fulladder_21_cout), .Sx(PC_4[22]), .Cout(fulladder_22_cout));
  FullAdder fulladder_23 (.Ax(A[23]), .Bx(B[23]), .Cin(fulladder_22_cout), .Sx(PC_4[23]));  // open: Cout

  // Other names for the same wires on the sheet: num15 = B[16]; num16 = B[17]; num17 = B[18]
endmodule

module main (
  output [31:0] out_1,
  output [3:0] out_2
);

  wire Branch, Clk, Halt, Imed, J_or_B_out_4, Jump, multiplexer_3_out, O, print, Reiniciar, W;
  wire [2:0] funct;
  wire [3:0] a, b, c;
  wire [15:0] MemInstrucoes_data;
  wire [23:0] extsinal_1_s, multiplexer_1_out, pc_1_out_5, somador24bits_1_pc_4, somador24bits_2_pc_4;
  wire [31:0] bancoregistrador32bits_1_a, bancoregistrador32bits_1_b, extzero_1_s, multiplexer_2_out,
       multiplexer_4_out, ula_1_c;

  somador24bits somador24bits_1 (.B(24'h1), .A(pc_1_out_5), .PC_4(somador24bits_1_pc_4));
  JorB J_or_B (.in_1(Jump), .in_2(O), .in_3(Branch), .out_4(J_or_B_out_4));
  ROM #(.addrWidth(24), .dataWidth(32)) MemInstrucoes (.addr(pc_1_out_5), .data({out_2, a, b, c, MemInstrucoes_data}));
  Multiplexer #(.width(24)) multiplexer_1 (
    .in0(somador24bits_1_pc_4), .in1(somador24bits_2_pc_4), .out(multiplexer_1_out), .sel(J_or_B_out_4));
  PC pc_1 (.Clock(Clk), .in_1(multiplexer_1_out), .Reiniciar(Reiniciar), .Halt(Halt), .out_5(pc_1_out_5));
  somador24bits somador24bits_2 (.B(extsinal_1_s), .A(pc_1_out_5), .PC_4(somador24bits_2_pc_4));
  extSinal extsinal_1 (.Imed(MemInstrucoes_data), .S(extsinal_1_s));
  Clock clock_1 (.out(Clk));
  Button button_1 (.out(Reiniciar));
  extZero extzero_1 (.Imed(MemInstrucoes_data), .S(extzero_1_s));
  ROM #(.addrWidth(4), .dataWidth(9)) MemControle (.addr(out_2), .data({funct, print, Branch, Jump, Imed, Halt, W}));
  BancoRegistrador32bits bancoregistrador32bits_1 (
    .C(ula_1_c), .Reiniciar(Reiniciar), .endA(a), .W(W), .endC(c), .Clock(Clk), .endB(b),
    .A(bancoregistrador32bits_1_a), .B(bancoregistrador32bits_1_b));
  Multiplexer #(.width(32)) multiplexer_2 (
    .in0(bancoregistrador32bits_1_a), .in1({32{1'b0}}), .out(multiplexer_2_out), .sel(Reiniciar));
  Multiplexer multiplexer_3 (.in0(print), .in1(1'b1), .out(multiplexer_3_out), .sel(Reiniciar));
  Multiplexer #(.width(32)) multiplexer_4 (
    .in0(bancoregistrador32bits_1_b), .in1(extzero_1_s), .out(multiplexer_4_out), .sel(Imed));
  registrador32 registrador32_1 (.Dado(multiplexer_2_out), .CLock(Clk), .Seletor(multiplexer_3_out), .Q(out_1));
  ULA ula_1 (.B(multiplexer_4_out), .A(bancoregistrador32bits_1_a), .Funct(funct), .out_4(O), .C(ula_1_c));

  // Notes on the sheet:
  //   contents of MemInstrucoes (hex, n*v repeats v):
  //   9001000a 90020007 90030012 900a0000 90040000 c4100007 44350000 22560000 2a6a0000 da000000 94040001
  //   b000fffa da000000 e0000000
  //   contents of MemControle (hex, n*v repeats v):
  //   0 5 1 101 81 181 41 141 c1 5 104 c 150 20 2
endmodule

module JorB (
  input  in_1,
  input  in_2,
  input  in_3,
  output out_4
);

  wire and_1_out;

  and and_1 (and_1_out, in_2, in_3);
  or or_1 (out_4, in_1, and_1_out);
endmodule
